# Fritzing sketch FanConexion (saved by Fritzing 0.8.5b)
breadboards: 1

parts:
  Parte1 = Arduino Mega 2560 (Rev3)
  JP2 = Header 4 [package=molex-1x4_lock]
  VCC1 = Battery block 9V
  R2 = Resistor [tolerance=±5% resistance=10k package=THT]

nets:
  N1: Parte1.D8_PWM, JP2.1
  N2: Parte1.5V, R2.Pin_1
  N3: Parte1.D48, JP2.2, R2.Pin_0
  N4: Parte1.GND, JP2.4, VCC1.-
  N5: JP2.3, VCC1.+

notes:
  To Computer fan
  - Black = Ground
  - Yellow = +12V or +9V
  - Blue = Tach signal (Open drain)
  - Green = PWM
